# Fritzing sketch RGB_led_int_control_w_pot_and_lcd (saved by Fritzing 0.9.10b)
breadboards: 1

parts:
  LED1 = RGB LED (com. cathode, rgb) [package="5 mm [THT]"]
  R1 = Resistor [tolerance=±5% resistance=220 package="2010 [SMD]"]
  R2 = Resistor [tolerance=±5% resistance=220 package="2010 [SMD]"]
  R3 = Resistor [tolerance=±5% resistance=220 package="2010 [SMD]"]
  U1 = POT [knob_status=50% power=0.5W package=pot_mammoth]
  LCD2 = LCD screen
  LCM1602_IIC2 = LCM1602 IIC [part_number="LCM1602 IIC" chip_label="LCM1602 IIC" package="DIP (Dual Inline) [THT]"]
  Mod1 = Raspberry Pi Pico  # not connected

nets:
  N1: LED1.red_anode, R1.Pin_1
  N2: LED1.common_cathode, U1.S, U1.A
  N3: LED1.green_anode, R2.Pin_1
  N4: LED1.blue_anode, R3.Pin_1
  VSS: LCD2.VSS, LCM1602_IIC2.VSS
  VDD: LCD2.VDD, LCM1602_IIC2.VDD
  N5: LCD2.V0, LCM1602_IIC2.V0
  N6: LCD2.RS, LCM1602_IIC2.RS
  N7: LCD2.R/W, LCM1602_IIC2.RW
  N8: LCD2.E, LCM1602_IIC2.E
  N9: LCD2.DB0, LCM1602_IIC2.D0
  N10: LCD2.DB1, LCM1602_IIC2.D1
  N11: LCD2.DB2, LCM1602_IIC2.D2
  N12: LCD2.DB3, LCM1602_IIC2.D3
  N13: LCD2.DB4, LCM1602_IIC2.D4
  N14: LCD2.DB5, LCM1602_IIC2.D5
  N15: LCD2.DB6, LCM1602_IIC2.D6
  N16: LCD2.DB7, LCM1602_IIC2.D7
  N17: LCD2.LED+, LCM1602_IIC2.A
  N18: LCD2.LED-, LCM1602_IIC2.K
  N19: LCM1602_IIC2.LED_A, LCM1602_IIC2.LED_B

custom parts:
  LCM1602 IIC: I2C-Module to use a 1602 or 2004 LCD on with the wire.h libory Serial LCD Modul
  Raspberry Pi Pico: Raspberry Pi Pico. Based around the RP2040 microcontroller the Pico is a low cost microcontroller device bringing Raspberry Pi quality, cost, and easy of use to the microcontroller space. Jan 2021, Split part in to two versions: SMD (this one) and tht. This one is single sided and uses the castellation pads to solder the module to the board (no holes, other than for the USB connector!). The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
